# Fritzing sketch Buttons (saved by Fritzing 1.0.8)
breadboards: 1

parts:
  S2 = Momentary Switch [package=ksa_sealed_tac_switch]
  R1 = Resistor [tolerance=±5% power=0.25W resistance=220 package=THT]
  R2 = Resistor [tolerance=±5% power=0.25W resistance=220 package=THT]
  Part1 = Arduino Uno (Rev3)
  S1 = Momentary Switch [package=ksa_sealed_tac_switch]
  R3 = Resistor [tolerance=±5% power=0.25W resistance=220 package=THT]
  LED1 = LED - 5mm [color="Orange (612nm)" current=0.030A package="5 mm [THT]"]

nets:
  N1: S2.1, Part1.5V, S1.1
  N2: S2.3, R1.Pin_0
  N3: S2.4, Part1.D8
  N4: R1.Pin_1, R2.Pin_1, Part1.GND, LED1.cathode
  N5: R2.Pin_0, S1.3
  N6: Part1.D11_PWM/MOSI, R3.Pin_0
  N7: Part1.D7, S1.4
  N8: R3.Pin_1, LED1.anode
