# Fritzing sketch Buzzer (saved by Fritzing 1.0.8)
breadboards: 1

parts:
  S2 = Momentary Switch [package=ksa_sealed_tac_switch]
  R1 = Resistor [tolerance=±5% power=0.25W resistance=220 package=THT]
  R2 = Resistor [tolerance=±5% power=0.25W resistance=220 package=THT]
  Part1 = Arduino Uno (Rev3)
  S1 = Momentary Switch [package=ksa_sealed_tac_switch]
  Piezo_Buzzer = Buzzer 12mm [part_number=COM-07950 package=buzzer-12mm-ns]

nets:
  N1: S2.1, Part1.5V, S1.1
  N2: S2.3, R1.Pin_0
  N3: S2.4, Part1.D8
  N4: R1.Pin_1, R2.Pin_1, Part1.GND, Piezo_Buzzer.2
  N5: R2.Pin_0, S1.3
  N6: Part1.D11_PWM/MOSI, Piezo_Buzzer.1
  N7: Part1.D7, S1.4

custom parts:
  Buzzer 12mm: Buzzer 12mm Spark Fun Electronics SKU : Comp-Buzzer Through hole This is a small 12mm round speaker that operates around the audible 2kHz range. You can use these speakers to create simple music or user interfaces. This is not a true piezoelectric speaker but behaves similarly. Instead of a piezoelectric crystal that vibrates with an electric current, this tiny speaker uses an electromagnet to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
