# Fritzing sketch DC Motor L293D Example (saved by Fritzing 1.0.8)
breadboards: 1

parts:
  IC1 = L293D [package=THT]
  M1 = DC Motor [voltage_(max)=6V voltage_(min)=3V]
  Part1 = Arduino Uno (Rev3) - ICSP
  Part2 = Breadboard Power Supply Board SMD

nets:
  N1: IC1.Enable_1, Part1.D10_PWM/SS
  N2: IC1.In_1, Part1.D9_PWM
  N3: IC1.Out_1_(_Controlled_by_Enable_1_), M1.pin_2
  GND: IC1.0V, Part1.GND, Part2.GND
  N4: IC1.Out_2_(_Controlled_by_Enable_1_), M1.pin_1
  N5: IC1.In_2, Part1.D7
  N6: IC1.+Vmotor, IC1.+V, Part2.VCC
