# Fritzing sketch Knob (saved by Fritzing 1.0.8)
breadboards: 1

parts:
  Part1 = Arduino Uno (Rev3)
  C1 = Capacitor Polarized [package=cpol-radial-10uf-25v]
  J1 = Basic Servo
  U1 = POT [knob_status=50% power=0.5W package=trim_pot]

nets:
  N1: Part1.D9_PWM, J1.pulse
  GND: Part1.GND, C1.-, J1.gnd, U1.S
  5V: Part1.5V, C1.+, J1.vcc, U1.A
