# Fritzing sketch UltraServo (saved by Fritzing 1.0.8)
breadboards: 1

parts:
  Part1 = Arduino Uno (Rev3)
  SEN1 = US-100 Ultrasonic Distance Sensor
  J1 = Basic Servo

nets:
  N1: Part1.D9_PWM, J1.pulse
  GND: Part1.GND, SEN1.GND, J1.gnd
  N2: Part1.D6_PWM, SEN1.ECHO
  N3: Part1.D7, SEN1.TRIG
  VCC: Part1.5V, SEN1.VCC, J1.vcc
